// Logisim project ALU.circ as structural Verilog: 10 circuits, main circuit alu_16
module halfadd (
  input  in_1,
  input  in_2,
  output carry,
  output sum
);

  and_x and_x_1 (.in_1(in_1), .in_2(in_2), .out_3(carry));
  xor_x xor_x_1 (.in_1(in_1), .in_2(in_2), .out_3(sum));
endmodule

module add (
  input  a,
  input  b,
  input  carry,
  output carry_2,
  output sum
);

  wire halfadd_1_carry, halfadd_1_sum, halfadd_2_carry;

  halfadd halfadd_1 (.in_1(a), .in_2(b), .sum(halfadd_1_sum), .carry(halfadd_1_carry));
  halfadd halfadd_2 (.in_1(halfadd_1_sum), .in_2(carry), .sum(sum), .carry(halfadd_2_carry));
  xor_x xor_x_1 (.in_1(halfadd_1_carry), .in_2(halfadd_2_carry), .out_3(carry_2));
endmodule

module add_x16 (
  input  [15:0] in_1,
  input  [15:0] in_2,
  output [15:0] out_3
);

  wire add_1_carry_2, add_2_carry_2, add_3_carry_2, add_4_carry_2, add_5_carry_2, add_6_carry_2,
       add_7_carry_2, add_8_carry_2, add_9_carry_2, add_10_carry_2, add_11_carry_2, add_12_carry_2,
       add_13_carry_2, add_14_carry_2, add_15_carry_2;

  add add_1 (.a(in_1[0]), .b(in_2[0]), .carry(1'b0), .carry_2(add_1_carry_2), .sum(out_3[0]));
  add add_2 (.a(in_1[1]), .b(add_1_carry_2), .carry(in_2[1]), .carry_2(add_2_carry_2), .sum(out_3[1]));
  add add_3 (.a(in_1[2]), .b(add_2_carry_2), .carry(in_2[2]), .carry_2(add_3_carry_2), .sum(out_3[2]));
  add add_4 (.a(in_1[3]), .b(add_3_carry_2), .carry(in_2[3]), .carry_2(add_4_carry_2), .sum(out_3[3]));
  add add_5 (.a(in_1[4]), .b(add_4_carry_2), .carry(in_2[4]), .carry_2(add_5_carry_2), .sum(out_3[4]));
  add add_6 (.a(in_1[5]), .b(add_5_carry_2), .carry(in_2[5]), .carry_2(add_6_carry_2), .sum(out_3[5]));
  add add_7 (.a(in_1[6]), .b(add_6_carry_2), .carry(in_2[6]), .carry_2(add_7_carry_2), .sum(out_3[6]));
  add add_8 (.a(in_1[7]), .b(add_7_carry_2), .carry(in_2[7]), .carry_2(add_8_carry_2), .sum(out_3[7]));
  add add_9 (.a(in_1[8]), .b(add_8_carry_2), .carry(in_2[8]), .carry_2(add_9_carry_2), .sum(out_3[8]));
  add add_10 (.a(in_1[9]), .b(add_9_carry_2), .carry(in_2[9]), .carry_2(add_10_carry_2), .sum(out_3[9]));
  add add_11 (.a(in_1[10]), .b(add_10_carry_2), .carry(in_2[10]), .carry_2(add_11_carry_2), .sum(out_3[10]));
  add add_12 (.a(in_1[11]), .b(add_11_carry_2), .carry(in_2[11]), .carry_2(add_12_carry_2), .sum(out_3[11]));
  add add_13 (.a(in_1[12]), .b(add_12_carry_2), .carry(in_2[12]), .carry_2(add_13_carry_2), .sum(out_3[12]));
  add add_14 (.a(in_1[13]), .b(add_13_carry_2), .carry(in_2[13]), .carry_2(add_14_carry_2), .sum(out_3[13]));
  add add_15 (.a(in_1[14]), .b(add_14_carry_2), .carry(in_2[14]), .carry_2(add_15_carry_2), .sum(out_3[14]));
  add add_16 (.a(in_1[15]), .b(add_15_carry_2), .carry(in_2[15]), .sum(out_3[15]));  // open: carry_2

  // Other names for the same wires on the sheet: A0 = in_1[0]; A1 = in_1[1]; A2 = in_1[2]; A3 = in_1[3]; A4 = in_1[4];
  //   A5 = in_1[5]; A6 = in_1[6]; A7 = in_1[7]; A8 = in_1[8]; A9 = in_1[9]; A10 = in_1[10]; A11 = in_1[11];
  //   A12 = in_1[12]; A13 = in_1[13]; A14 = in_1[14]; A15 = in_1[15]; B0 = in_2[0]; B1 = in_2[1]; B2 = in_2[2];
  //   B3 = in_2[3]; B4 = in_2[4]; B5 = in_2[5]; B6 = in_2[6]; B7 = in_2[7]; B8 = in_2[8]; B9 = in_2[9];
  //   B10 = in_2[10]; B11 = in_2[11]; B12 = in_2[12]; B13 = in_2[13]; B14 = in_2[14]; B15 = in_2[15]
endmodule

module inc_x16 (
  input  [15:0] in_1,
  output [15:0] out_2
);

  add_x16 add_x16_1 (.in_1(in_1), .in_2(16'h1), .out_3(out_2));
endmodule

module neg_x16 (
  input  [15:0] in_1,
  output [15:0] out_2
);

  wire [15:0] not_x16_1_out_2;

  not_x16 not_x16_1 (.in_1(in_1), .out_2(not_x16_1_out_2));
  inc_x16 inc_x16_1 (.in_1(not_x16_1_out_2), .out_2(out_2));
endmodule

module sub_x16 (
  input  [15:0] in_1,
  input  [15:0] in_2,
  output [15:0] out_3
);

  wire [15:0] neg_x16_1_out_2;

  neg_x16 neg_x16_1 (.in_1(in_2), .out_2(neg_x16_1_out_2));
  add_x16 add_x16_1 (.in_1(in_1), .in_2(neg_x16_1_out_2), .out_3(out_3));
endmodule

module desc_x16 (
  input  [15:0] in_1,
  output [15:0] out_2
);

  wire [15:0] neg_x16_1_out_2;

  neg_x16 neg_x16_1 (.in_1(16'h1), .out_2(neg_x16_1_out_2));
  add_x16 add_x16_1 (.in_1(in_1), .in_2(neg_x16_1_out_2), .out_3(out_2));
endmodule

module logicunit_x16 (
  input  [15:0] in_1,
  input  [1:0] Op_code,
  input  [15:0] in_3,
  output [15:0] out_4
);

  wire A2, B2, undriven;
  wire [15:0] and_x16_1_out_3, not_x16_1_out_2, or_x16_1_out_3, xor_x16_1_out_3;

  not_x16 not_x16_1 (.in_1(in_1), .out_2(not_x16_1_out_2));
  xor_x16 xor_x16_1 (.in_2(in_3), .in_1(in_1), .out_3(xor_x16_1_out_3));
  mux4_x16 mux4_x16_1 (
    .in_5(Op_code), .in_1(not_x16_1_out_2), .in_2(xor_x16_1_out_3), .in_3(or_x16_1_out_3),
    .in_4(and_x16_1_out_3), .out_6(out_4));
  or_x16 or_x16_1 (.in_1(in_1), .in_2(in_3), .out_3(or_x16_1_out_3));
  and_x16 and_x16_1 (.in_2(in_3), .in_1(in_1), .out_3(and_x16_1_out_3));
  add add_1 (.a(A2), .b(undriven), .carry(B2));  // open: carry_2, sum

  // Other names for the same wires on the sheet: A[15:0] = in_1; B[15:0] = in_3
endmodule

module arithmeticunit_x16 (
  input  [15:0] in_1,
  input  [1:0] Op_code,
  input  [15:0] in_3,
  output [15:0] out_4
);

  wire [15:0] add_x16_1_out_3, desc_x16_1_out_2, inc_x16_1_out_2, sub_x16_1_out_3;

  desc_x16 desc_x16_1 (.in_1(in_1), .out_2(desc_x16_1_out_2));
  sub_x16 sub_x16_1 (.in_1(in_1), .in_2(in_3), .out_3(sub_x16_1_out_3));
  inc_x16 inc_x16_1 (.in_1(in_1), .out_2(inc_x16_1_out_2));
  mux4_x16 mux4_x16_1 (
    .in_5(Op_code), .in_1(desc_x16_1_out_2), .in_2(sub_x16_1_out_3), .in_3(inc_x16_1_out_2),
    .in_4(add_x16_1_out_3), .out_6(out_4));
  add_x16 add_x16_1 (.in_1(in_1), .in_2(in_3), .out_3(add_x16_1_out_3));

  // Other names for the same wires on the sheet: A[15:0] = in_1; B[15:0] = in_3
endmodule

module alu_16 (
  input  u,
  input  in_2,
  input  in_3,
  input  [1:0] Op_code,
  input  [15:0] y,
  input  [15:0] in_6,
  output [15:0] out_7
);

  wire [15:0] arithmeticunit_x16_1_out_4, logicunit_x16_1_out_4, mux_x16_2_out_4, mux_x16_3_out_4,
       mux_x16_4_out_4;

  mux_x16 mux_x16_1 (.in_1(u), .in_2(arithmeticunit_x16_1_out_4), .in_3(logicunit_x16_1_out_4), .out_4(out_7));
  arithmeticunit_x16 arithmeticunit_x16_1 (
    .in_1(mux_x16_2_out_4), .in_3(mux_x16_4_out_4), .Op_code(Op_code), .out_4(arithmeticunit_x16_1_out_4));
  mux_x16 mux_x16_2 (.in_1(in_2), .in_2({16{1'b0}}), .in_3(mux_x16_3_out_4), .out_4(mux_x16_2_out_4));
  mux_x16 mux_x16_3 (.in_1(in_3), .in_2(in_6), .in_3(y), .out_4(mux_x16_3_out_4));
  logicunit_x16 logicunit_x16_1 (
    .in_1(mux_x16_2_out_4), .in_3(mux_x16_4_out_4), .Op_code(Op_code), .out_4(logicunit_x16_1_out_4));
  mux_x16 mux_x16_4 (.in_1(in_3), .in_2(y), .in_3(in_6), .out_4(mux_x16_4_out_4));

  // Notes on the sheet:
  //   zx
  //   sw
  //   x'
  //   x
  //   y'
endmodule
