// Logisim project PC.circ as structural Verilog: 2 circuits, main circuit VonNeumannPC_x16
module VonNeumannPC_x16 (
  input  in_1,
  input  [15:0] _0x0007,
  input  [15:0] _0x0006,
  input  [15:0] _0x0005,
  input  [15:0] _0x0004,
  input  [15:0] _0x0003,
  input  [15:0] _0x0002,
  input  [15:0] _0x0001,
  input  [15:0] _0x0000
);

  wire ALU_or_Data, dmux8_1_out_3, dmux8_1_out_4, dmux8_1_out_5, dmux8_1_out_6, dmux8_1_out_7, dmux8_1_out_8,
       dmux8_1_out_9, dmux8_1_out_10, dmux_x_1_c0, dmux_x_1_c1, EQ, GE, GT, LE, LT, mux8_1_out_10,
       mux_x_1_out_4, mux_x_2_out_4, mux_x_3_out_4, NE, output2A;
  wire [1:0] rom_1_data_3;
  wire [2:0] rom_1_data;
  wire [14:0] alu_16_1_out_7;
  wire [14:3] rom_1_data_2;
  wire [15:0] alu_out, mem_out, mux_x16_1_out_4, pc_x16_1_out_4, ram_1_dout, ReadControl_out_10,
       reg_x16_1_out_4, regA;

  // Probe on {ALU_or_Data, rom_1_data_2[14:10], rom_1_data_3, rom_1_data_2[7:3], rom_1_data}
  // Probe on nothing
  mux8 mux8_1 (
    .in_9(rom_1_data), .in_1(1'b1), .in_2(LE), .in_3(NE), .in_4(LT), .in_5(GE), .in_6(EQ), .in_7(GT),
    .out_10(mux8_1_out_10));  // open: in_8
  mux_x16 mux_x16_1 (.in_1(rom_1_data_2[12]), .in_2(mem_out), .in_3(regA), .out_4(mux_x16_1_out_4));
  alu_16 alu_16_1 (
    .Op_code(rom_1_data_3), .in_2(rom_1_data_2[7]), .in_3(rom_1_data_2[6]), .y(reg_x16_1_out_4),
    .in_6(mux_x16_1_out_4), .u(rom_1_data_2[10]), .out_7({LT, alu_16_1_out_7}));
  or16_x or16_x_1 (.in_1({LT, alu_16_1_out_7}), .out_2(NE));
  not_x not_x_1 (.in_1(LT), .out_2(GE));
  not_x not_x_2 (.in_1(NE), .out_2(EQ));
  // Probe on {ALU_or_Data, rom_1_data_2[14:10], rom_1_data_3, rom_1_data_2[7:3], rom_1_data}
  or_x or_x_1 (.in_1(EQ), .in_2(LT), .out_3(LE));
  ROM #(.addrWidth(16), .dataWidth(16)) rom_1 (
    .addr(pc_x16_1_out_4),
    .data({ALU_or_Data, rom_1_data_2[14:10], rom_1_data_3, rom_1_data_2[7:3], rom_1_data}));
  // Probe on mux_x_1_out_4
  mux_x mux_x_1 (.Select(ALU_or_Data), .D1(mux8_1_out_10), .D0(1'b0), .out_4(mux_x_1_out_4));
  mux_x16 mux_x16_2 (
    .in_1(ALU_or_Data), .in_2({LT, alu_16_1_out_7}),
    .in_3({ALU_or_Data, rom_1_data_2[14:10], rom_1_data_3, rom_1_data_2[7:3], rom_1_data}), .out_4(alu_out));
  mux_x mux_x_2 (.Select(ALU_or_Data), .D1(rom_1_data_2[5]), .D0(1'b1), .out_4(mux_x_2_out_4));
  mux_x mux_x_3 (.Select(ALU_or_Data), .D1(rom_1_data_2[4]), .D0(1'b0), .out_4(mux_x_3_out_4));
  mux_x mux_x_4 (.Select(ALU_or_Data), .D1(rom_1_data_2[3]), .D0(1'b0), .out_4(output2A));
  not_x not_x_3 (.in_1(LE), .out_2(GT));
  // Probe on alu_out
  // Probe on mux_x_2_out_4
  // Probe on mux_x_3_out_4
  // Probe on output2A
  // Probe on pc_x16_1_out_4
  reg_x16 reg_x16_1 (.in_1(in_1), .load(mux_x_3_out_4), .data(alu_out), .out_4(reg_x16_1_out_4));
  reg_x16 reg_x16_2 (.in_1(in_1), .load(mux_x_2_out_4), .data(alu_out), .out_4(regA));
  pc_x16 pc_x16_1 (.load(mux_x_1_out_4), .in_3(regA), .in_1(in_1), .out_4(pc_x16_1_out_4));
  // Probe on reg_x16_1_out_4
  // Probe on regA
  dmux8 dmux8_1 (
    .in_2(dmux_x_1_c1), .in_1(regA[2:0]), .out_4(dmux8_1_out_4), .out_5(dmux8_1_out_5),
    .out_6(dmux8_1_out_6), .out_7(dmux8_1_out_7), .out_8(dmux8_1_out_8), .out_9(dmux8_1_out_9),
    .out_10(dmux8_1_out_10), .out_3(dmux8_1_out_3));
  dmux_x dmux_x_1 (.select(regA[14]), .in_2(output2A), .C1(dmux_x_1_c1), .C0(dmux_x_1_c0));
  // Probe on regA[13:0]
  RAM #(.addrWidth(14), .asyncread("true"), .dataWidth(16), .trigger("falling")) ram_1 (
    .addr(regA[13:0]), .we(dmux_x_1_c0), .oe(1'b1), .clk(in_1), .din(alu_out), .dout(ram_1_dout));
  reg_x16 reg_x16_3 (.in_1(in_1), .load(dmux8_1_out_3), .data(alu_out), .out_4(_0x0007));
  reg_x16 reg_x16_4 (.in_1(in_1), .load(dmux8_1_out_4), .data(alu_out), .out_4(_0x0006));
  reg_x16 reg_x16_5 (.in_1(in_1), .load(dmux8_1_out_5), .data(alu_out), .out_4(_0x0005));
  reg_x16 reg_x16_6 (.in_1(in_1), .load(dmux8_1_out_6), .data(alu_out), .out_4(_0x0004));
  reg_x16 reg_x16_7 (.in_1(in_1), .load(dmux8_1_out_7), .data(alu_out), .out_4(_0x0003));
  reg_x16 reg_x16_8 (.in_1(in_1), .load(dmux8_1_out_8), .data(alu_out), .out_4(_0x0002));
  reg_x16 reg_x16_9 (.in_1(in_1), .load(dmux8_1_out_9), .data(alu_out), .out_4(_0x0001));
  reg_x16 reg_x16_10 (.in_1(in_1), .load(dmux8_1_out_10), .data(alu_out), .out_4(_0x0000));
  // Probe on _0x0007
  // Probe on _0x0006
  // Probe on _0x0005
  // Probe on _0x0004
  // Probe on _0x0003
  // Probe on _0x0002
  // Probe on _0x0001
  // Probe on _0x0000
  mux8_x16 ReadControl (
    .in_9(regA[2:0]), .in_1(_0x0007), .in_2(_0x0006), .in_3(_0x0005), .in_4(_0x0004), .in_5(_0x0003),
    .in_6(_0x0002), .in_7(_0x0001), .in_8(_0x0000), .out_10(ReadControl_out_10));
  mux_x16 mux_x16_3 (.in_1(regA[14]), .in_2(ReadControl_out_10), .in_3(ram_1_dout), .out_4(mem_out));
  // Probe on ReadControl_out_10
  // Probe on ram_1_dout

  // Other names for the same wires on the sheet: clk = in_1; IO0[15:0] = _0x0000; IO1[15:0] = _0x0001;
  //   IO2[15:0] = _0x0002; IO3[15:0] = _0x0003; IO4[15:0] = _0x0004; IO5[15:0] = _0x0005; IO6[15:0] = _0x0006;
  //   IO7[15:0] = _0x0007

  // Notes on the sheet:
  //   Instruction
  //   Reg D
  //   A*
  //   Reg A
  //   (ALU) Jump Flag
  //   (ALU) Result
  //   (ALU) output to A flag
  //   ( ALU) output to D flag
  //   (ALU) output to A*
  //   contents of rom_1 (hex, n*v repeats v):
  //   0 8490 10 84c8 40 8490 11 84c8 100 8490 12 84c8 ff 8490 13 84c8 ff 8490 14 84c8 ff 8490 15 84c8 4000
  //   8588 8088 4006 8088 10 9490 4001 84c8 11 9490 4002 84c8 13 9490 4003 84c8 14 9490 4004 84c8 15 9490
  //   4005 84c8 4006 8588 8088 10 9548 12 9748 9490 1d 84c1 3b 8087
  //   memory data at address
  //   address
  //   Reg A
  //   D
  //   A
endmodule

module mcu_x16 (
);

  wire rgb_video_1_p2;
  wire [0:0] rgb_video_1_p3;
  wire [6:0] rgb_video_1_p5;
  wire [7:0] rgb_video_1_p4, undriven, undriven_3, undriven_4, undriven_5;
  wire [8:0] undriven_2;
  wire [14:0] undriven_6;
  wire [15:0] rgb_video_1_p1;
  wire [23:0] rgb_video_1_p6;

  // RGB_Video #(.width(256)) rgb_video_1: pin names not known; wires that end beside it: rgb_video_1_p1[0], rgb_video_1_p2, rgb_video_1_p3[0], rgb_video_1_p4, rgb_video_1_p5, rgb_video_1_p6
  VonNeumannPC_x16 vonneumannpc_x16_1 (
    ._0x0006({undriven, rgb_video_1_p4}), ._0x0005({undriven_2, rgb_video_1_p5}),
    ._0x0004({undriven_3, rgb_video_1_p6[7:0]}), ._0x0003({undriven_4, rgb_video_1_p6[15:8]}),
    ._0x0002({undriven_5, rgb_video_1_p6[23:16]}), ._0x0001({undriven_6, rgb_video_1_p3[0]}),
    ._0x0007(rgb_video_1_p1), .in_1(rgb_video_1_p2));  // open: _0x0000
  Clock clock_1 (.out(rgb_video_1_p2));

  // Notes on the sheet:
  //   R
  //   G
  //   B
endmodule
