// Logisim project basic.circ as structural Verilog
module nand_x (
  input  in_1,
  input  in_2,
  output out_3
);

  nand nand_1 (out_3, in_1, in_2);
endmodule

module not_x (
  input  in_1,
  output out_2
);

  nand nand_1 (out_2, in_1, in_1);
endmodule

module and_x (
  input  in_1,
  input  in_2,
  output out_3
);

  wire nand_1_out;

  nand nand_1 (nand_1_out, in_1, in_2);
  not_x not_x_1 (.in_1(nand_1_out), .out_2(out_3));
endmodule

module or_x (
  input  in_1,
  input  in_2,
  output out_3
);

  wire not_x_1_out_2, not_x_2_out_2;

  not_x not_x_1 (.in_1(in_1), .out_2(not_x_1_out_2));
  not_x not_x_2 (.in_1(in_2), .out_2(not_x_2_out_2));
  nand nand_1 (out_3, not_x_1_out_2, not_x_2_out_2);
endmodule

module or16_x (
  input  [15:0] in_1,
  output out_2
);

  wire or_x_1_out_3, or_x_2_out_3, or_x_3_out_3, or_x_4_out_3, or_x_5_out_3, or_x_6_out_3, or_x_7_out_3,
       or_x_8_out_3, or_x_9_out_3, or_x_10_out_3, or_x_11_out_3, or_x_13_out_3, or_x_14_out_3, or_x_15_out_3;

  or_x or_x_1 (.in_1(in_1[0]), .in_2(in_1[1]), .out_3(or_x_1_out_3));
  or_x or_x_2 (.in_1(or_x_1_out_3), .in_2(in_1[2]), .out_3(or_x_2_out_3));
  or_x or_x_3 (.in_1(or_x_15_out_3), .in_2(in_1[10]), .out_3(or_x_3_out_3));
  or_x or_x_4 (.in_1(or_x_3_out_3), .in_2(in_1[11]), .out_3(or_x_4_out_3));
  or_x or_x_5 (.in_1(or_x_2_out_3), .in_2(in_1[3]), .out_3(or_x_5_out_3));
  or_x or_x_6 (.in_1(or_x_5_out_3), .in_2(in_1[4]), .out_3(or_x_6_out_3));
  or_x or_x_7 (.in_1(or_x_4_out_3), .in_2(in_1[12]), .out_3(or_x_7_out_3));
  or_x or_x_8 (.in_1(or_x_6_out_3), .in_2(in_1[5]), .out_3(or_x_8_out_3));
  or_x or_x_9 (.in_1(or_x_7_out_3), .in_2(in_1[13]), .out_3(or_x_9_out_3));
  or_x or_x_10 (.in_1(or_x_8_out_3), .in_2(in_1[6]), .out_3(or_x_10_out_3));
  or_x or_x_11 (.in_1(or_x_9_out_3), .in_2(in_1[14]), .out_3(or_x_11_out_3));
  or_x or_x_12 (.in_1(or_x_11_out_3), .in_2(in_1[15]), .out_3(out_2));
  or_x or_x_13 (.in_1(or_x_10_out_3), .in_2(in_1[7]), .out_3(or_x_13_out_3));
  or_x or_x_14 (.in_1(or_x_13_out_3), .in_2(in_1[8]), .out_3(or_x_14_out_3));
  or_x or_x_15 (.in_1(or_x_14_out_3), .in_2(in_1[9]), .out_3(or_x_15_out_3));
endmodule

module xor_x (
  input  in_1,
  input  in_2,
  output out_3
);

  wire and_x_1_out_3, and_x_2_out_3, not_x_1_out_2, not_x_2_out_2;

  not_x not_x_1 (.in_1(in_1), .out_2(not_x_1_out_2));
  and_x and_x_1 (.in_1(not_x_1_out_2), .in_2(in_2), .out_3(and_x_1_out_3));
  not_x not_x_2 (.in_1(in_2), .out_2(not_x_2_out_2));
  and_x and_x_2 (.in_1(not_x_2_out_2), .in_2(in_1), .out_3(and_x_2_out_3));
  or_x or_x_1 (.in_1(and_x_1_out_3), .in_2(and_x_2_out_3), .out_3(out_3));
endmodule

module mux_x (
  input  Select,
  input  D1,
  input  D0,
  output out_4
);

  wire and_x_1_out_3, and_x_2_out_3, not_x_1_out_2;

  not_x not_x_1 (.in_1(Select), .out_2(not_x_1_out_2));
  and_x and_x_1 (.in_1(not_x_1_out_2), .in_2(D0), .out_3(and_x_1_out_3));
  and_x and_x_2 (.in_1(D1), .in_2(Select), .out_3(and_x_2_out_3));
  or_x or_x_1 (.in_1(and_x_1_out_3), .in_2(and_x_2_out_3), .out_3(out_4));
endmodule

module dmux_x (
  input  select,
  input  in_2,
  output C1,
  output C0
);

  wire not_x_1_out_2;

  not_x not_x_1 (.in_1(select), .out_2(not_x_1_out_2));
  and_x and_x_1 (.in_1(select), .in_2(in_2), .out_3(C1));
  and_x and_x_2 (.in_1(not_x_1_out_2), .in_2(in_2), .out_3(C0));
endmodule

module mux4 (
  input  in_1,
  input  in_2,
  input  in_3,
  input  in_4,
  input  [1:0] in_5,
  output out_6
);

  wire mux_x_2_out_4, mux_x_3_out_4;

  mux_x mux_x_1 (.Select(in_5[1]), .D1(mux_x_2_out_4), .D0(mux_x_3_out_4), .out_4(out_6));
  mux_x mux_x_2 (.Select(in_5[0]), .D1(in_1), .D0(in_2), .out_4(mux_x_2_out_4));
  mux_x mux_x_3 (.Select(in_5[0]), .D1(in_3), .D0(in_4), .out_4(mux_x_3_out_4));
endmodule

module mux8 (
  input  in_1,
  input  in_2,
  input  in_3,
  input  in_4,
  input  in_5,
  input  in_6,
  input  in_7,
  input  in_8,
  input  [2:0] in_9,
  output out_10
);

  wire mux4_1_out_6, mux4_2_out_6;

  mux_x mux_x_1 (.Select(in_9[2]), .D1(mux4_1_out_6), .D0(mux4_2_out_6), .out_4(out_10));
  mux4 mux4_1 (.in_5(in_9[1:0]), .in_1(in_1), .in_2(in_2), .in_3(in_3), .in_4(in_4), .out_6(mux4_1_out_6));
  mux4 mux4_2 (.in_5(in_9[1:0]), .in_1(in_5), .in_2(in_6), .in_3(in_7), .in_4(in_8), .out_6(mux4_2_out_6));
endmodule

module dmux4 (
  input  [1:0] in_1,
  input  in_2,
  output out_3,
  output out_4,
  output out_5,
  output out_6
);

  wire dmux_x_1_c0, dmux_x_1_c1;

  dmux_x dmux_x_1 (.select(in_1[1]), .in_2(in_2), .C1(dmux_x_1_c1), .C0(dmux_x_1_c0));
  dmux_x dmux_x_2 (.select(in_1[0]), .in_2(dmux_x_1_c1), .C1(out_3), .C0(out_4));
  dmux_x dmux_x_3 (.select(in_1[0]), .in_2(dmux_x_1_c0), .C1(out_5), .C0(out_6));
endmodule

module dmux8 (
  input  [2:0] in_1,
  input  in_2,
  output out_3,
  output out_4,
  output out_5,
  output out_6,
  output out_7,
  output out_8,
  output out_9,
  output out_10
);

  wire dmux_x_1_c0, dmux_x_1_c1;

  dmux_x dmux_x_1 (.select(in_1[2]), .in_2(in_2), .C1(dmux_x_1_c1), .C0(dmux_x_1_c0));
  dmux4 dmux4_1 (.in_2(dmux_x_1_c1), .in_1(in_1[1:0]), .out_3(out_3), .out_4(out_4), .out_5(out_5), .out_6(out_6));
  dmux4 dmux4_2 (.in_2(dmux_x_1_c0), .in_1(in_1[1:0]), .out_3(out_7), .out_4(out_8), .out_5(out_9), .out_6(out_10));
endmodule

module not_x16 (
  input  [15:0] in_1,
  output [15:0] out_2
);

  not_x not_x_1 (.in_1(in_1[0]), .out_2(out_2[0]));
  not_x not_x_2 (.in_1(in_1[1]), .out_2(out_2[1]));
  not_x not_x_3 (.in_1(in_1[2]), .out_2(out_2[2]));
  not_x not_x_4 (.in_1(in_1[3]), .out_2(out_2[3]));
  not_x not_x_5 (.in_1(in_1[4]), .out_2(out_2[4]));
  not_x not_x_6 (.in_1(in_1[5]), .out_2(out_2[5]));
  not_x not_x_7 (.in_1(in_1[6]), .out_2(out_2[6]));
  not_x not_x_8 (.in_1(in_1[7]), .out_2(out_2[7]));
  not_x not_x_9 (.in_1(in_1[8]), .out_2(out_2[8]));
  not_x not_x_10 (.in_1(in_1[9]), .out_2(out_2[9]));
  not_x not_x_11 (.in_1(in_1[10]), .out_2(out_2[10]));
  not_x not_x_12 (.in_1(in_1[11]), .out_2(out_2[11]));
  not_x not_x_13 (.in_1(in_1[12]), .out_2(out_2[12]));
  not_x not_x_14 (.in_1(in_1[13]), .out_2(out_2[13]));
  not_x not_x_15 (.in_1(in_1[14]), .out_2(out_2[14]));
  not_x not_x_16 (.in_1(in_1[15]), .out_2(out_2[15]));
endmodule

module and_x16 (
  input  [15:0] in_1,
  input  [15:0] in_2,
  output [15:0] out_3
);

  and_x and_x_1 (.in_1(in_1[0]), .in_2(in_2[0]), .out_3(out_3[0]));
  and_x and_x_2 (.in_1(in_1[1]), .in_2(in_2[1]), .out_3(out_3[1]));
  and_x and_x_3 (.in_1(in_1[2]), .in_2(in_2[2]), .out_3(out_3[2]));
  and_x and_x_4 (.in_1(in_1[3]), .in_2(in_2[3]), .out_3(out_3[3]));
  and_x and_x_5 (.in_1(in_1[4]), .in_2(in_2[4]), .out_3(out_3[4]));
  and_x and_x_6 (.in_1(in_1[5]), .in_2(in_2[5]), .out_3(out_3[5]));
  and_x and_x_7 (.in_1(in_1[6]), .in_2(in_2[6]), .out_3(out_3[6]));
  and_x and_x_8 (.in_1(in_1[7]), .in_2(in_2[7]), .out_3(out_3[7]));
  and_x and_x_9 (.in_1(in_1[8]), .in_2(in_2[8]), .out_3(out_3[8]));
  and_x and_x_10 (.in_1(in_1[9]), .in_2(in_2[9]), .out_3(out_3[9]));
  and_x and_x_11 (.in_1(in_1[10]), .in_2(in_2[10]), .out_3(out_3[10]));
  and_x and_x_12 (.in_1(in_1[11]), .in_2(in_2[11]), .out_3(out_3[11]));
  and_x and_x_13 (.in_1(in_1[12]), .in_2(in_2[12]), .out_3(out_3[12]));
  and_x and_x_14 (.in_1(in_1[13]), .in_2(in_2[13]), .out_3(out_3[13]));
  and_x and_x_15 (.in_1(in_1[14]), .in_2(in_2[14]), .out_3(out_3[14]));
  and_x and_x_16 (.in_1(in_1[15]), .in_2(in_2[15]), .out_3(out_3[15]));
endmodule

module or_x16 (
  input  [15:0] in_1,
  input  [15:0] in_2,
  output [15:0] out_3
);

  or_x or_x_1 (.in_1(in_1[0]), .in_2(in_2[0]), .out_3(out_3[0]));
  or_x or_x_2 (.in_1(in_1[1]), .in_2(in_2[1]), .out_3(out_3[1]));
  or_x or_x_3 (.in_1(in_1[2]), .in_2(in_2[2]), .out_3(out_3[2]));
  or_x or_x_4 (.in_1(in_1[3]), .in_2(in_2[3]), .out_3(out_3[3]));
  or_x or_x_5 (.in_1(in_1[4]), .in_2(in_2[4]), .out_3(out_3[4]));
  or_x or_x_6 (.in_1(in_1[5]), .in_2(in_2[5]), .out_3(out_3[5]));
  or_x or_x_7 (.in_1(in_1[6]), .in_2(in_2[6]), .out_3(out_3[6]));
  or_x or_x_8 (.in_1(in_1[7]), .in_2(in_2[7]), .out_3(out_3[7]));
  or_x or_x_9 (.in_1(in_1[8]), .in_2(in_2[8]), .out_3(out_3[8]));
  or_x or_x_10 (.in_1(in_1[9]), .in_2(in_2[9]), .out_3(out_3[9]));
  or_x or_x_11 (.in_1(in_1[10]), .in_2(in_2[10]), .out_3(out_3[10]));
  or_x or_x_12 (.in_1(in_1[11]), .in_2(in_2[11]), .out_3(out_3[11]));
  or_x or_x_13 (.in_1(in_1[12]), .in_2(in_2[12]), .out_3(out_3[12]));
  or_x or_x_14 (.in_1(in_1[13]), .in_2(in_2[13]), .out_3(out_3[13]));
  or_x or_x_15 (.in_1(in_1[14]), .in_2(in_2[14]), .out_3(out_3[14]));
  or_x or_x_16 (.in_1(in_1[15]), .in_2(in_2[15]), .out_3(out_3[15]));
endmodule

module xor_x16 (
  input  [15:0] in_1,
  input  [15:0] in_2,
  output [15:0] out_3
);

  xor_x xor_x_1 (.in_1(in_1[0]), .in_2(in_2[0]), .out_3(out_3[0]));
  xor_x xor_x_2 (.in_1(in_1[1]), .in_2(in_2[1]), .out_3(out_3[1]));
  xor_x xor_x_3 (.in_1(in_1[2]), .in_2(in_2[2]), .out_3(out_3[2]));
  xor_x xor_x_4 (.in_1(in_1[3]), .in_2(in_2[3]), .out_3(out_3[3]));
  xor_x xor_x_5 (.in_1(in_1[4]), .in_2(in_2[4]), .out_3(out_3[4]));
  xor_x xor_x_6 (.in_1(in_1[5]), .in_2(in_2[5]), .out_3(out_3[5]));
  xor_x xor_x_7 (.in_1(in_1[6]), .in_2(in_2[6]), .out_3(out_3[6]));
  xor_x xor_x_8 (.in_1(in_1[7]), .in_2(in_2[7]), .out_3(out_3[7]));
  xor_x xor_x_9 (.in_1(in_1[8]), .in_2(in_2[8]), .out_3(out_3[8]));
  xor_x xor_x_10 (.in_1(in_1[9]), .in_2(in_2[9]), .out_3(out_3[9]));
  xor_x xor_x_11 (.in_1(in_1[10]), .in_2(in_2[10]), .out_3(out_3[10]));
  xor_x xor_x_12 (.in_1(in_1[11]), .in_2(in_2[11]), .out_3(out_3[11]));
  xor_x xor_x_13 (.in_1(in_1[12]), .in_2(in_2[12]), .out_3(out_3[12]));
  xor_x xor_x_14 (.in_1(in_1[13]), .in_2(in_2[13]), .out_3(out_3[13]));
  xor_x xor_x_15 (.in_1(in_1[14]), .in_2(in_2[14]), .out_3(out_3[14]));
  xor_x xor_x_16 (.in_1(in_1[15]), .in_2(in_2[15]), .out_3(out_3[15]));
endmodule

module mux_x16 (
  input  in_1,
  input  [15:0] in_2,
  input  [15:0] in_3,
  output [15:0] out_4
);

  mux_x mux_x_1 (.Select(in_1), .D1(in_2[15]), .D0(in_3[15]), .out_4(out_4[15]));
  mux_x mux_x_2 (.Select(in_1), .D1(in_2[14]), .D0(in_3[14]), .out_4(out_4[14]));
  mux_x mux_x_3 (.Select(in_1), .D1(in_2[13]), .D0(in_3[13]), .out_4(out_4[13]));
  mux_x mux_x_4 (.Select(in_1), .D1(in_2[12]), .D0(in_3[12]), .out_4(out_4[12]));
  mux_x mux_x_5 (.Select(in_1), .D1(in_2[11]), .D0(in_3[11]), .out_4(out_4[11]));
  mux_x mux_x_6 (.Select(in_1), .D1(in_2[10]), .D0(in_3[10]), .out_4(out_4[10]));
  mux_x mux_x_7 (.Select(in_1), .D1(in_2[9]), .D0(in_3[9]), .out_4(out_4[9]));
  mux_x mux_x_8 (.Select(in_1), .D1(in_2[8]), .D0(in_3[8]), .out_4(out_4[8]));
  mux_x mux_x_9 (.Select(in_1), .D1(in_2[7]), .D0(in_3[7]), .out_4(out_4[7]));
  mux_x mux_x_10 (.Select(in_1), .D1(in_2[6]), .D0(in_3[6]), .out_4(out_4[6]));
  mux_x mux_x_11 (.Select(in_1), .D1(in_2[5]), .D0(in_3[5]), .out_4(out_4[5]));
  mux_x mux_x_12 (.Select(in_1), .D1(in_2[4]), .D0(in_3[4]), .out_4(out_4[4]));
  mux_x mux_x_13 (.Select(in_1), .D1(in_2[3]), .D0(in_3[3]), .out_4(out_4[3]));
  mux_x mux_x_14 (.Select(in_1), .D1(in_2[2]), .D0(in_3[2]), .out_4(out_4[2]));
  mux_x mux_x_15 (.Select(in_1), .D1(in_2[1]), .D0(in_3[1]), .out_4(out_4[1]));
  mux_x mux_x_16 (.Select(in_1), .D1(in_2[0]), .D0(in_3[0]), .out_4(out_4[0]));
endmodule

module mux4_x16 (
  input  [15:0] in_1,
  input  [15:0] in_2,
  input  [15:0] in_3,
  input  [15:0] in_4,
  input  [1:0] in_5,
  output [15:0] out_6
);

  wire [15:0] mux_x16_2_out_4, mux_x16_3_out_4;

  mux_x16 mux_x16_1 (.in_1(in_5[1]), .in_2(mux_x16_2_out_4), .in_3(mux_x16_3_out_4), .out_4(out_6));
  mux_x16 mux_x16_2 (.in_1(in_5[0]), .in_2(in_1), .in_3(in_2), .out_4(mux_x16_2_out_4));
  mux_x16 mux_x16_3 (.in_1(in_5[0]), .in_2(in_3), .in_3(in_4), .out_4(mux_x16_3_out_4));
endmodule

module mux8_x16 (
  input  [15:0] in_1,
  input  [15:0] in_2,
  input  [15:0] in_3,
  input  [15:0] in_4,
  input  [15:0] in_5,
  input  [15:0] in_6,
  input  [15:0] in_7,
  input  [15:0] in_8,
  input  [2:0] in_9,
  output [15:0] out_10
);

  wire [15:0] mux4_x16_1_out_6, mux4_x16_2_out_6;

  mux_x16 mux_x16_1 (.in_1(in_9[2]), .in_2(mux4_x16_1_out_6), .in_3(mux4_x16_2_out_6), .out_4(out_10));
  mux4_x16 mux4_x16_1 (.in_5(in_9[1:0]), .in_1(in_1), .in_2(in_2), .in_3(in_3), .in_4(in_4), .out_6(mux4_x16_1_out_6));
  mux4_x16 mux4_x16_2 (.in_5(in_9[1:0]), .in_1(in_5), .in_2(in_6), .in_3(in_7), .in_4(in_8), .out_6(mux4_x16_2_out_6));
endmodule

module dmux_x16 (
  input  in_1,
  input  [15:0] in_2,
  output [15:0] out_3,
  output [15:0] out_4
);

  dmux_x dmux_x_1 (.select(in_1), .in_2(in_2[14]), .C1(out_3[14]), .C0(out_4[14]));
  dmux_x dmux_x_2 (.select(in_1), .in_2(in_2[15]), .C1(out_3[15]), .C0(out_4[15]));
  dmux_x dmux_x_3 (.select(in_1), .in_2(in_2[13]), .C1(out_3[13]), .C0(out_4[13]));
  dmux_x dmux_x_4 (.select(in_1), .in_2(in_2[11]), .C1(out_3[11]), .C0(out_4[11]));
  dmux_x dmux_x_5 (.select(in_1), .in_2(in_2[12]), .C1(out_3[12]), .C0(out_4[12]));
  dmux_x dmux_x_6 (.select(in_1), .in_2(in_2[10]), .C1(out_3[10]), .C0(out_4[10]));
  dmux_x dmux_x_7 (.select(in_1), .in_2(in_2[8]), .C1(out_3[8]), .C0(out_4[8]));
  dmux_x dmux_x_8 (.select(in_1), .in_2(in_2[9]), .C1(out_3[9]), .C0(out_4[9]));
  dmux_x dmux_x_9 (.select(in_1), .in_2(in_2[6]), .C1(out_3[6]), .C0(out_4[6]));
  dmux_x dmux_x_10 (.select(in_1), .in_2(in_2[7]), .C1(out_3[7]), .C0(out_4[7]));
  dmux_x dmux_x_11 (.select(in_1), .in_2(in_2[5]), .C1(out_3[5]), .C0(out_4[5]));
  dmux_x dmux_x_12 (.select(in_1), .in_2(in_2[3]), .C1(out_3[3]), .C0(out_4[3]));
  dmux_x dmux_x_13 (.select(in_1), .in_2(in_2[4]), .C1(out_3[4]), .C0(out_4[4]));
  dmux_x dmux_x_14 (.select(in_1), .in_2(in_2[2]), .C1(out_3[2]), .C0(out_4[2]));
  dmux_x dmux_x_15 (.select(in_1), .in_2(in_2[0]), .C1(out_3[0]), .C0(out_4[0]));
  dmux_x dmux_x_16 (.select(in_1), .in_2(in_2[1]), .C1(out_3[1]), .C0(out_4[1]));

  // Other names for the same wires on the sheet: I0 = in_2[0]; I1 = in_2[1]; I2 = in_2[2]; I3 = in_2[3]; I4 = in_2[4];
  //   I5 = in_2[5]; I6 = in_2[6]; I7 = in_2[7]; I8 = in_2[8]; I9 = in_2[9]; I10 = in_2[10]; I11 = in_2[11];
  //   I12 = in_2[12]; I13 = in_2[13]; I14 = in_2[14]; I15 = in_2[15]; D1_0 = out_3[0]; D1_1 = out_3[1];
  //   D1_2 = out_3[2]; D1_3 = out_3[3]; D1_4 = out_3[4]; D1_5 = out_3[5]; D1_6 = out_3[6]; D1_7 = out_3[7];
  //   D1_8 = out_3[8]; D1_9 = out_3[9]; D1_10 = out_3[10]; D1_11 = out_3[11]; D1_12 = out_3[12]; D1_13 = out_3[13];
  //   D1_14 = out_3[14]; D1_15 = out_3[15]; D0_0 = out_4[0]; D0_1 = out_4[1]; D0_2 = out_4[2]; D0_3 = out_4[3];
  //   D0_4 = out_4[4]; D0_5 = out_4[5]; D0_6 = out_4[6]; D0_7 = out_4[7]; D0_8 = out_4[8]; D0_9 = out_4[9];
  //   D0_10 = out_4[10]; D0_11 = out_4[11]; D0_12 = out_4[12]; D0_13 = out_4[13]; D0_14 = out_4[14];
  //   D0_15 = out_4[15]
endmodule

module dmux4_x16 (
  input  [1:0] in_1,
  input  [15:0] in_2,
  output [15:0] out_3,
  output [15:0] out_4,
  output [15:0] out_5,
  output [15:0] out_6
);

  wire [15:0] dmux_x16_1_out_3, dmux_x16_1_out_4;

  dmux_x16 dmux_x16_1 (.in_1(in_1[1]), .in_2(in_2), .out_3(dmux_x16_1_out_3), .out_4(dmux_x16_1_out_4));
  dmux_x16 dmux_x16_2 (.in_1(in_1[0]), .in_2(dmux_x16_1_out_3), .out_3(out_3), .out_4(out_4));
  dmux_x16 dmux_x16_3 (.in_1(in_1[0]), .in_2(dmux_x16_1_out_4), .out_3(out_5), .out_4(out_6));
endmodule

module dmux8_x16 (
  input  [2:0] in_1,
  input  [15:0] in_2,
  output [15:0] out_3,
  output [15:0] out_4,
  output [15:0] out_5,
  output [15:0] out_6,
  output [15:0] out_7,
  output [15:0] out_8,
  output [15:0] out_9,
  output [15:0] out_10
);

  wire [15:0] dmux_x16_1_out_3, dmux_x16_1_out_4;

  dmux_x16 dmux_x16_1 (.in_1(in_1[2]), .in_2(in_2), .out_3(dmux_x16_1_out_3), .out_4(dmux_x16_1_out_4));
  dmux4_x16 dmux4_x16_1 (
    .in_2(dmux_x16_1_out_3), .in_1(in_1[1:0]), .out_3(out_3), .out_4(out_4), .out_5(out_5), .out_6(out_6));
  dmux4_x16 dmux4_x16_2 (
    .in_2(dmux_x16_1_out_4), .in_1(in_1[1:0]), .out_3(out_7), .out_4(out_8), .out_5(out_9), .out_6(out_10));
endmodule

module ini_basic (
  input  [2:0] in_1,
  input  in_2,
  input  [15:0] in_3,
  input  [15:0] in_4,
  input  [15:0] in_5,
  input  [15:0] in_6,
  input  [15:0] in_7,
  input  [15:0] in_8,
  input  [15:0] in_9,
  input  in_10,
  input  [15:0] in_11,
  input  [15:0] in_12,
  input  [1:0] in_13,
  input  [15:0] in_14,
  input  [15:0] in_15,
  input  [15:0] in_16,
  input  [15:0] in_17,
  input  [2:0] in_18,
  input  [15:0] in_19,
  input  [15:0] in_20,
  input  [15:0] in_21,
  input  [15:0] in_22,
  input  [15:0] in_23,
  input  [15:0] in_24,
  input  [15:0] in_25,
  input  [15:0] in_26,
  input  in_27,
  input  [15:0] in_28,
  input  [1:0] in_29,
  input  [15:0] in_30,
  input  [2:0] in_31,
  input  [15:0] in_32
);

  wire [15:0] and_vhd_x16_1_o, dmux4_vhd_x16_1_o0, dmux4_vhd_x16_1_o1, dmux4_vhd_x16_1_o2,
       dmux4_vhd_x16_1_o3, dmux8_vhd_x16_1_o0, dmux8_vhd_x16_1_o1, dmux8_vhd_x16_1_o2, dmux8_vhd_x16_1_o3,
       dmux8_vhd_x16_1_o4, dmux8_vhd_x16_1_o5, dmux8_vhd_x16_1_o6, dmux8_vhd_x16_1_o7, dmux_vhd_x16_1_o0,
       dmux_vhd_x16_1_o1, mux4_vhd_x16_1_o, mux8_vhd_x16_1_o, mux_hdl_x16_1_o, not_vhd_x16_1_o,
       or_vhd_x16_1_o, xor_vhd_x16_1_o;

  nand_vhd_x nand_vhd_x_1 ();  // open: A, B, Y
  not_vhd_x not_vhd_x_1 ();  // open: I, O
  and_vhd_x and_vhd_x_1 ();  // open: A, B, Y
  or_vhd_x or_vhd_x_1 ();  // open: A, B, O
  not_zero_vhd_x16 not_zero_vhd_x16_1 ();  // open: I, O
  xor_vhd_x xor_vhd_x_1 ();  // open: A, B, O
  mux_vhd_x mux_vhd_x_1 ();  // open: S, D1, D0, O
  dmux_vhd_x dmux_vhd_x_1 ();  // open: S, D, O1, O0
  mux4_vhd_x mux4_vhd_x_1 ();  // open: S, I3, I2, I1, I0, O
  mux8_vhd_x mux8_vhd_x_1 ();  // open: S, I7, I6, I5, I4, I3, I2, I1, I0, O
  dmux4_vhd_x dmux4_vhd_x_1 ();  // open: S, I, O3, O2, O1, O0
  dmux8_vhd_x dmux8_vhd_x_1 (.S(in_1), .I(in_2));  // open: O7, O6, O5, O4, O3, O2, O1, O0
  // Probe on not_vhd_x16_1_o
  not_vhd_x16 not_vhd_x16_1 (.I(in_3), .O(not_vhd_x16_1_o));
  // Probe on and_vhd_x16_1_o
  and_vhd_x16 and_vhd_x16_1 (.A(in_4), .B(in_5), .O(and_vhd_x16_1_o));
  // Probe on or_vhd_x16_1_o
  or_vhd_x16 or_vhd_x16_1 (.A(in_6), .B(in_7), .O(or_vhd_x16_1_o));
  // Probe on xor_vhd_x16_1_o
  xor_vhd_x16 xor_vhd_x16_1 (.A(in_8), .B(in_9), .O(xor_vhd_x16_1_o));
  // Probe on mux_hdl_x16_1_o
  mux_hdl_x16 mux_hdl_x16_1 (.S(in_10), .D1(in_11), .D0(in_12), .O(mux_hdl_x16_1_o));
  // Probe on mux4_vhd_x16_1_o
  mux4_vhd_x16 mux4_vhd_x16_1 (.S(in_13), .D3(in_14), .D2(in_15), .D1(in_16), .D0(in_17), .O(mux4_vhd_x16_1_o));
  // Probe on mux8_vhd_x16_1_o
  mux8_vhd_x16 mux8_vhd_x16_1 (
    .S(in_18), .D7(in_19), .D6(in_20), .D5(in_21), .D4(in_22), .D3(in_23), .D2(in_24), .D1(in_25),
    .D0(in_26), .O(mux8_vhd_x16_1_o));
  // Probe on dmux_vhd_x16_1_o1
  dmux_vhd_x16 dmux_vhd_x16_1 (.S(in_27), .D(in_28), .O1(dmux_vhd_x16_1_o1), .O0(dmux_vhd_x16_1_o0));
  // Probe on dmux_vhd_x16_1_o0
  // Probe on dmux4_vhd_x16_1_o3
  dmux4_vhd_x16 dmux4_vhd_x16_1 (
    .S(in_29), .D(in_30), .O3(dmux4_vhd_x16_1_o3), .O2(dmux4_vhd_x16_1_o2), .O1(dmux4_vhd_x16_1_o1),
    .O0(dmux4_vhd_x16_1_o0));
  // Probe on dmux4_vhd_x16_1_o2
  // Probe on dmux4_vhd_x16_1_o1
  // Probe on dmux4_vhd_x16_1_o0
  // Probe on dmux8_vhd_x16_1_o7
  dmux8_vhd_x16 dmux8_vhd_x16_1 (
    .S(in_31), .D(in_32), .O7(dmux8_vhd_x16_1_o7), .O6(dmux8_vhd_x16_1_o6), .O5(dmux8_vhd_x16_1_o5),
    .O4(dmux8_vhd_x16_1_o4), .O3(dmux8_vhd_x16_1_o3), .O2(dmux8_vhd_x16_1_o2), .O1(dmux8_vhd_x16_1_o1),
    .O0(dmux8_vhd_x16_1_o0));
  // Probe on dmux8_vhd_x16_1_o6
  // Probe on dmux8_vhd_x16_1_o5
  // Probe on dmux8_vhd_x16_1_o4
  // Probe on dmux8_vhd_x16_1_o3
  // Probe on dmux8_vhd_x16_1_o2
  // Probe on dmux8_vhd_x16_1_o1
  // Probe on dmux8_vhd_x16_1_o0
endmodule

// VHDL entity nand_vhd_x, as the project stores it:
library IEEE;
use IEEE.std_logic_1164.all;

entity nand_vhd_x is
    Port (
        A: in   STD_LOGIC;
        B: in   STD_LOGIC;
        Y: out  STD_LOGIC
    );
end nand_vhd_x;

architecture default of nand_vhd_x is
begin
    Y <= not (A and B);
end default;

// VHDL entity not_vhd_x, as the project stores it:
library IEEE;
use IEEE.std_logic_1164.all;

entity not_vhd_x is
    Port (
        I: in   STD_LOGIC;
        O: out  STD_LOGIC
    );
end not_vhd_x;

architecture default of not_vhd_x is
    component nand_vhd_x
        Port (
            A: in   STD_LOGIC;
            B: in   STD_LOGIC;
            Y: out  STD_LOGIC
        );
    end component;
begin
    connect: nand_vhd_x port map (I, I, O);
end default;

// VHDL entity and_vhd_x, as the project stores it:
library IEEE;
use IEEE.std_logic_1164.all;

entity and_vhd_x is
    Port (
        A: in   STD_LOGIC;
        B: in   STD_LOGIC;
        Y: out  STD_LOGIC
    );
end and_vhd_x;

architecture default of and_vhd_x is
    component nand_vhd_x
        Port (
            A: in   STD_LOGIC;
            B: in   STD_LOGIC;
            Y: out  STD_LOGIC
        );
    end component;
    component not_vhd_x
        Port (
            I: in   STD_LOGIC;
            O: out  STD_LOGIC
        );
    end component;

    signal NAND_O: STD_LOGIC;
    
begin
    connection1: nand_vhd_x port map (A, B, NAND_O);
    connection2: not_vhd_x port map (NAND_O, Y);
end default;

// VHDL entity or_vhd_x, as the project stores it:
library IEEE;
use IEEE.std_logic_1164.all;

entity or_vhd_x is
    Port (
        A: in   STD_LOGIC;
        B: in   STD_LOGIC;
        O: out  STD_LOGIC
    );
end or_vhd_x;

architecture default of or_vhd_x is
    component nand_vhd_x
        Port (
            A: in   STD_LOGIC;
            B: in   STD_LOGIC;
            Y: out  STD_LOGIC
        );
    end component;
    component not_vhd_x
        Port (
            I: in   STD_LOGIC;
            O: out  STD_LOGIC
        );
    end component;

    signal NOT_A: STD_LOGIC;
    signal NOT_B: STD_LOGIC;

begin
    reverse_a   : not_vhd_x port map (A, NOT_A);
    reverse_b   : not_vhd_x port map (B, NOT_B);
    nand_ab     : nand_vhd_x port map (NOT_A, NOT_B, O);
end default;

// VHDL entity not_zero_vhd_x16, as the project stores it:
library IEEE;
use IEEE.std_logic_1164.all;

entity not_zero_vhd_x16 is
    Port (
        I: in   STD_LOGIC_VECTOR (15 downto 0);
        O: out  STD_LOGIC
    );
end not_zero_vhd_x16;

architecture default of not_zero_vhd_x16 is
    component or_vhd_x
        Port (
            A: in   STD_LOGIC;
            B: in   STD_LOGIC;
            O: out  STD_LOGIC
        );
    end component;

    signal OR1: STD_LOGIC;
    signal OR2: STD_LOGIC;
    signal OR3: STD_LOGIC;
    signal OR4: STD_LOGIC;
    signal OR5: STD_LOGIC;
    signal OR6: STD_LOGIC;
    signal OR7: STD_LOGIC;
    signal OR8: STD_LOGIC;
    signal OR9: STD_LOGIC;
    signal OR10: STD_LOGIC;
    signal OR11: STD_LOGIC;
    signal OR12: STD_LOGIC;
    signal OR13: STD_LOGIC;
    signal OR14: STD_LOGIC;
    signal OR15: STD_LOGIC;

begin
    or_1:   or_vhd_x port map (I(0), I(1), OR1);
    or_2:   or_vhd_x port map (OR1, I(2), OR2);
    or_3:   or_vhd_x port map (OR2, I(3), OR3);
    or_4:   or_vhd_x port map (OR3, I(4), OR4);
    or_5:   or_vhd_x port map (OR4, I(5), OR5);
    or_6:   or_vhd_x port map (OR5, I(6), OR6);
    or_7:   or_vhd_x port map (OR6, I(7), OR7);
    or_8:   or_vhd_x port map (OR7, I(8), OR8);
    or_9:   or_vhd_x port map (OR8, I(9), OR9);
    or_10:  or_vhd_x port map (OR9, I(10), OR10);
    or_11:  or_vhd_x port map (OR10, I(11), OR11);
    or_12:  or_vhd_x port map (OR11, I(12), OR12);
    or_13:  or_vhd_x port map (OR12, I(13), OR13);
    or_14:  or_vhd_x port map (OR13, I(14), OR14);
    or_15:  or_vhd_x port map (OR14, I(15), OR15);
    O <= OR15;
end default;

// VHDL entity xor_vhd_x, as the project stores it:
library IEEE;
use IEEE.std_logic_1164.all;

entity xor_vhd_x is
    Port (
        A: in   STD_LOGIC;
        B: in   STD_LOGIC;
        O: out  STD_LOGIC
    );
end xor_vhd_x;

architecture default of xor_vhd_x is
    component not_vhd_x
        Port (
            I: in   STD_LOGIC;
            O: out  STD_LOGIC
        );
    end component;
    component and_vhd_x
        Port (
            A: in   STD_LOGIC;
            B: in   STD_LOGIC;
            Y: out  STD_LOGIC
        );
    end component;
    component or_vhd_x
        Port (
            A: in   STD_LOGIC;
            B: in   STD_LOGIC;
            O: out  STD_LOGIC
        );
    end component;

    signal NOT_A: STD_LOGIC;
    signal NOT_B: STD_LOGIC;
    signal NOT_A_AND_B: STD_LOGIC;
    signal NOT_B_AND_A: STD_LOGIC;

begin
    reverse_a   : not_vhd_x port map (A, NOT_A);
    reverse_b   : not_vhd_x port map (B, NOT_B);
    and1        : and_vhd_x port map (NOT_A, B, NOT_A_AND_B);
    and2        : and_vhd_x port map (A, NOT_B, NOT_B_AND_A);
    last        : or_vhd_x  port map (NOT_A_AND_B, NOT_B_AND_A, O);
end default;

// VHDL entity mux_vhd_x, as the project stores it:
library IEEE;
use IEEE.std_logic_1164.all;

entity mux_vhd_x is
    Port (
        S   : in    STD_LOGIC;
        D1  : in    STD_LOGIC;
        D0  : in    STD_LOGIC;
        O   : out   STD_LOGIC
    );
end mux_vhd_x;

architecture default of mux_vhd_x is
    component not_vhd_x
        Port (
            I: in   STD_LOGIC;
            O: out  STD_LOGIC
        );
    end component;
    component and_vhd_x
        Port (
            A: in   STD_LOGIC;
            B: in   STD_LOGIC;
            Y: out  STD_LOGIC
        );
    end component;
    component or_vhd_x
        Port (
            A: in   STD_LOGIC;
            B: in   STD_LOGIC;
            O: out  STD_LOGIC
        );
    end component;

    signal NOT_SELECT        : STD_LOGIC;
    signal NOT_SELECT_AND_D0 : STD_LOGIC;
    signal SELECT_AND_D1     : STD_LOGIC;

begin
    reverse_s : not_vhd_x port map (S, NOT_SELECT);
    data0     : and_vhd_x port map (NOT_SELECT, D0, NOT_SELECT_AND_D0);
    data1     : and_vhd_x port map (S, D1, SELECT_AND_D1);
    last      : or_vhd_x  port map (NOT_SELECT_AND_D0, SELECT_AND_D1, O);
end default;

// VHDL entity dmux_vhd_x, as the project stores it:
library IEEE;
use IEEE.std_logic_1164.all;

entity dmux_vhd_x is
    Port (
        S: in   STD_LOGIC;
        D: in   STD_LOGIC;
        O1: out  STD_LOGIC;
        O0: out  STD_LOGIC
    );
end dmux_vhd_x;

architecture default of dmux_vhd_x is
    component not_vhd_x
        Port (
            I: in   STD_LOGIC;
            O: out  STD_LOGIC
        );
    end component;
    component and_vhd_x
        Port (
            A: in   STD_LOGIC;
            B: in   STD_LOGIC;
            Y: out  STD_LOGIC
        );
    end component;

    signal NOT_SELECT: STD_LOGIC;

begin
    reverse_s : not_vhd_x port map (S, NOT_SELECT);
    low_bit   : and_vhd_x port map (NOT_SELECT, D, O0);
    high_bit  : and_vhd_x port map (S, D, O1);
end default;

// VHDL entity mux4_vhd_x, as the project stores it:
library IEEE;
use IEEE.std_logic_1164.all;

entity mux4_vhd_x is
    Port (
        S   : in    STD_LOGIC_VECTOR (1 downto 0);
        I3  : in    STD_LOGIC;
        I2  : in    STD_LOGIC;
        I1  : in    STD_LOGIC;
        I0  : in    STD_LOGIC;
        O   : out   STD_LOGIC
    );
end mux4_vhd_x;

architecture default of mux4_vhd_x is
    component mux_vhd_x is
        Port (
            S   : in    STD_LOGIC;
            D1  : in    STD_LOGIC;
            D0  : in    STD_LOGIC;
            O   : out   STD_LOGIC
        );
    end component;

    signal H: STD_LOGIC;
    signal L: STD_LOGIC;

begin
    get_high : mux_vhd_x port map (S(0), I3, I2, H);
    get_low  : mux_vhd_x port map (S(0), I1, I0, L);
    last     : mux_vhd_x port map (S(1), H, L, O);
end default;

// VHDL entity mux8_vhd_x, as the project stores it:
library IEEE;
use IEEE.std_logic_1164.all;

entity mux8_vhd_x is
    Port (
        S   : in    STD_LOGIC_VECTOR (2 downto 0);
        I7  : in    STD_LOGIC;
        I6  : in    STD_LOGIC;
        I5  : in    STD_LOGIC;
        I4  : in    STD_LOGIC;
        I3  : in    STD_LOGIC;
        I2  : in    STD_LOGIC;
        I1  : in    STD_LOGIC;
        I0  : in    STD_LOGIC;
        O   : out   STD_LOGIC
    );
end mux8_vhd_x;

architecture default of mux8_vhd_x is
    component mux_vhd_x is
        Port (
            S   : in    STD_LOGIC;
            D1  : in    STD_LOGIC;
            D0  : in    STD_LOGIC;
            O   : out   STD_LOGIC
        );
    end component;
    component mux4_vhd_x is
        Port (
            S   : in    STD_LOGIC_VECTOR (1 downto 0);
            I3  : in    STD_LOGIC;
            I2  : in    STD_LOGIC;
            I1  : in    STD_LOGIC;
            I0  : in    STD_LOGIC;
            O   : out   STD_LOGIC
        );
    end component;

    signal H: STD_LOGIC;
    signal L: STD_LOGIC;

begin
    get_high: mux4_vhd_x port map (S(1 downto 0), I7, I6, I5, I4, H);
    get_low : mux4_vhd_x port map (S(1 downto 0), I3, I2, I1, I0, L);
    last    : mux_vhd_x  port map (S(2), H, L, O);
end default;

// VHDL entity dmux4_vhd_x, as the project stores it:
library IEEE;
use IEEE.std_logic_1164.all;

entity dmux4_vhd_x is
    Port (
        S   : in    STD_LOGIC_VECTOR (1 downto 0);
        I   : in    STD_LOGIC;
        O3  : out   STD_LOGIC;
        O2  : out   STD_LOGIC;
        O1  : out   STD_LOGIC;
        O0  : out   STD_LOGIC
    );
end dmux4_vhd_x;

architecture default of dmux4_vhd_x is
    component dmux_vhd_x is
        Port (
            S: in   STD_LOGIC;
            D: in   STD_LOGIC;
            O1: out  STD_LOGIC;
            O0: out  STD_LOGIC
        );
    end component;

    signal H: STD_LOGIC;
    signal L: STD_LOGIC;

begin
    locate      : dmux_vhd_x port map (S(1), I, H, L);
    output_high : dmux_vhd_x port map (S(0), H, O3, O2);
    output_low  : dmux_vhd_x port map (S(0), L, O1, O0);
end default;

// VHDL entity dmux8_vhd_x, as the project stores it:
library IEEE;
use IEEE.std_logic_1164.all;

entity dmux8_vhd_x is
    Port (
        S   : in  STD_LOGIC_VECTOR (2 downto 0);
        I   : in  STD_LOGIC;
        O7  : out STD_LOGIC;
        O6  : out STD_LOGIC;
        O5  : out STD_LOGIC;
        O4  : out STD_LOGIC;
        O3  : out STD_LOGIC;
        O2  : out STD_LOGIC;
        O1  : out STD_LOGIC;
        O0  : out STD_LOGIC
    );
end dmux8_vhd_x;

architecture default of dmux8_vhd_x is
    component dmux_vhd_x is
        Port (
            S: in   STD_LOGIC;
            D: in   STD_LOGIC;
            O1: out  STD_LOGIC;
            O0: out  STD_LOGIC
        );
    end component;
    component dmux4_vhd_x is
        Port (
            S   : in    STD_LOGIC_VECTOR (1 downto 0);
            I   : in    STD_LOGIC;
            O3  : out   STD_LOGIC;
            O2  : out   STD_LOGIC;
            O1  : out   STD_LOGIC;
            O0  : out   STD_LOGIC
        );
    end component;

    signal H: STD_LOGIC;
    signal L: STD_LOGIC;
    
begin
    locate      : dmux_vhd_x port map (S(2), I, H, L);
    output_high : dmux4_vhd_x port map (S(1 downto 0), H, O7, O6, O5, O4);
    output_low  : dmux4_vhd_x port map (S(1 downto 0), L, O3, O2, O1, O0);
end architecture default;

// VHDL entity not_vhd_x16, as the project stores it:
library IEEE;
use IEEE.std_logic_1164.all;

entity not_vhd_x16 is
    Port (
        I: in   STD_LOGIC_VECTOR (15 downto 0);
        O: out  STD_LOGIC_VECTOR (15 downto 0)
    );
end not_vhd_x16;

architecture default of not_vhd_x16 is
    component not_vhd_x is
        Port (
            I: in   STD_LOGIC;
            O: out  STD_LOGIC
        );
    end component;

    -- signal NOT_0: STD_LOGIC;
    -- signal NOT_1: STD_LOGIC;
    -- signal NOT_2: STD_LOGIC;
    -- signal NOT_3: STD_LOGIC;
    -- signal NOT_4: STD_LOGIC;
    -- signal NOT_5: STD_LOGIC;
    -- signal NOT_6: STD_LOGIC;
    -- signal NOT_7: STD_LOGIC;
    -- signal NOT_8: STD_LOGIC;
    -- signal NOT_9: STD_LOGIC;
    -- signal NOT_10: STD_LOGIC;
    -- signal NOT_11: STD_LOGIC;
    -- signal NOT_12: STD_LOGIC;
    -- signal NOT_13: STD_LOGIC;
    -- signal NOT_14: STD_LOGIC;
    -- signal NOT_15: STD_LOGIC;

begin
    reverse_0: not_vhd_x port map (I(0), O(0));
    reverse_1: not_vhd_x port map (I(1), O(1));
    reverse_2: not_vhd_x port map (I(2), O(2));
    reverse_3: not_vhd_x port map (I(3), O(3));
    reverse_4: not_vhd_x port map (I(4), O(4));
    reverse_5: not_vhd_x port map (I(5), O(5));
    reverse_6: not_vhd_x port map (I(6), O(6));
    reverse_7: not_vhd_x port map (I(7), O(7));
    reverse_8: not_vhd_x port map (I(8), O(8));
    reverse_9: not_vhd_x port map (I(9), O(9));
    reverse_10: not_vhd_x port map (I(10), O(10));
    reverse_11: not_vhd_x port map (I(11), O(11));
    reverse_12: not_vhd_x port map (I(12), O(12));
    reverse_13: not_vhd_x port map (I(13), O(13));
    reverse_14: not_vhd_x port map (I(14), O(14));
    reverse_15: not_vhd_x port map (I(15), O(15));
end default;

// VHDL entity and_vhd_x16, as the project stores it:
library IEEE;
use IEEE.std_logic_1164.all;

entity and_vhd_x16 is
    Port (
        A: in   STD_LOGIC_VECTOR (15 downto 0);
        B: in   STD_LOGIC_VECTOR (15 downto 0);
        O: out  STD_LOGIC_VECTOR (15 downto 0)
    );
end and_vhd_x16;

architecture default of and_vhd_x16 is
    component and_vhd_x is
        Port (
            A: in   STD_LOGIC;
            B: in   STD_LOGIC;
            Y: out  STD_LOGIC
        );
    end component;

begin
    and_0: and_vhd_x port map (A(0), B(0), O(0));
    and_1: and_vhd_x port map (A(1), B(1), O(1));
    and_2: and_vhd_x port map (A(2), B(2), O(2));
    and_3: and_vhd_x port map (A(3), B(3), O(3));
    and_4: and_vhd_x port map (A(4), B(4), O(4));
    and_5: and_vhd_x port map (A(5), B(5), O(5));
    and_6: and_vhd_x port map (A(6), B(6), O(6));
    and_7: and_vhd_x port map (A(7), B(7), O(7));
    and_8: and_vhd_x port map (A(8), B(8), O(8));
    and_9: and_vhd_x port map (A(9), B(9), O(9));
    and_10: and_vhd_x port map (A(10), B(10), O(10));
    and_11: and_vhd_x port map (A(11), B(11), O(11));
    and_12: and_vhd_x port map (A(12), B(12), O(12));
    and_13: and_vhd_x port map (A(13), B(13), O(13));
    and_14: and_vhd_x port map (A(14), B(14), O(14));
    and_15: and_vhd_x port map (A(15), B(15), O(15));
end default;

// VHDL entity or_vhd_x16, as the project stores it:
library IEEE;
use IEEE.std_logic_1164.all;

entity or_vhd_x16 is
    Port (
        A: in   STD_LOGIC_VECTOR (15 downto 0);
        B: in   STD_LOGIC_VECTOR (15 downto 0);
        O: out  STD_LOGIC_VECTOR (15 downto 0)
    );
end or_vhd_x16;

architecture default of or_vhd_x16 is
    component or_vhd_x is
        Port (
            A: in   STD_LOGIC;
            B: in   STD_LOGIC;
            O: out  STD_LOGIC
        );
    end component;

begin
    or_0: or_vhd_x port map (A(0), B(0), O(0));
    or_1: or_vhd_x port map (A(1), B(1), O(1));
    or_2: or_vhd_x port map (A(2), B(2), O(2));
    or_3: or_vhd_x port map (A(3), B(3), O(3));
    or_4: or_vhd_x port map (A(4), B(4), O(4));
    or_5: or_vhd_x port map (A(5), B(5), O(5));
    or_6: or_vhd_x port map (A(6), B(6), O(6));
    or_7: or_vhd_x port map (A(7), B(7), O(7));
    or_8: or_vhd_x port map (A(8), B(8), O(8));
    or_9: or_vhd_x port map (A(9), B(9), O(9));
    or_10: or_vhd_x port map (A(10), B(10), O(10));
    or_11: or_vhd_x port map (A(11), B(11), O(11));
    or_12: or_vhd_x port map (A(12), B(12), O(12));
    or_13: or_vhd_x port map (A(13), B(13), O(13));
    or_14: or_vhd_x port map (A(14), B(14), O(14));
    or_15: or_vhd_x port map (A(15), B(15), O(15));
end default;

// VHDL entity xor_vhd_x16, as the project stores it:
library IEEE;
use IEEE.std_logic_1164.all;

entity xor_vhd_x16 is
    Port (
        A: in   STD_LOGIC_VECTOR (15 downto 0);
        B: in   STD_LOGIC_VECTOR (15 downto 0);
        O: out  STD_LOGIC_VECTOR (15 downto 0)
    );
end xor_vhd_x16;

architecture default of xor_vhd_x16 is
    component xor_vhd_x is
        Port (
            A: in   STD_LOGIC;
            B: in   STD_LOGIC;
            O: out  STD_LOGIC
        );
    end component;

begin
    xor_1: xor_vhd_x port map (A(1), B(1), O(1));
    xor_0: xor_vhd_x port map (A(0), B(0), O(0));
    xor_2: xor_vhd_x port map (A(2), B(2), O(2));
    xor_3: xor_vhd_x port map (A(3), B(3), O(3));
    xor_4: xor_vhd_x port map (A(4), B(4), O(4));
    xor_5: xor_vhd_x port map (A(5), B(5), O(5));
    xor_6: xor_vhd_x port map (A(6), B(6), O(6));
    xor_7: xor_vhd_x port map (A(7), B(7), O(7));
    xor_8: xor_vhd_x port map (A(8), B(8), O(8));
    xor_9: xor_vhd_x port map (A(9), B(9), O(9));
    xor_10: xor_vhd_x port map (A(10), B(10), O(10));
    xor_11: xor_vhd_x port map (A(11), B(11), O(11));
    xor_12: xor_vhd_x port map (A(12), B(12), O(12));
    xor_13: xor_vhd_x port map (A(13), B(13), O(13));
    xor_14: xor_vhd_x port map (A(14), B(14), O(14));
    xor_15: xor_vhd_x port map (A(15), B(15), O(15));
end default;

// VHDL entity mux_hdl_x16, as the project stores it:
library IEEE;
use IEEE.std_logic_1164.all;

entity mux_hdl_x16 is
    Port (
        S:  in  STD_LOGIC;
        D1: in  STD_LOGIC_VECTOR (15 downto 0);
        D0: in  STD_LOGIC_VECTOR (15 downto 0);
        O:  out STD_LOGIC_VECTOR (15 downto 0)
    );
end mux_hdl_x16;

architecture default of mux_hdl_x16 is
    component mux_vhd_x is
        Port (
            S   : in    STD_LOGIC;
            D1  : in    STD_LOGIC;
            D0  : in    STD_LOGIC;
            O   : out   STD_LOGIC
        );
    end component;

begin
    mux_0: mux_vhd_x port map (S, D1(0), D0(0), O(0));
    mux_1: mux_vhd_x port map (S, D1(1), D0(1), O(1));
    mux_2: mux_vhd_x port map (S, D1(2), D0(2), O(2));
    mux_3: mux_vhd_x port map (S, D1(3), D0(3), O(3));
    mux_4: mux_vhd_x port map (S, D1(4), D0(4), O(4));
    mux_5: mux_vhd_x port map (S, D1(5), D0(5), O(5));
    mux_6: mux_vhd_x port map (S, D1(6), D0(6), O(6));
    mux_7: mux_vhd_x port map (S, D1(7), D0(7), O(7));
    mux_8: mux_vhd_x port map (S, D1(8), D0(8), O(8));
    mux_9: mux_vhd_x port map (S, D1(9), D0(9), O(9));
    mux_10: mux_vhd_x port map (S, D1(10), D0(10), O(10));
    mux_11: mux_vhd_x port map (S, D1(11), D0(11), O(11));
    mux_12: mux_vhd_x port map (S, D1(12), D0(12), O(12));
    mux_13: mux_vhd_x port map (S, D1(13), D0(13), O(13));
    mux_14: mux_vhd_x port map (S, D1(14), D0(14), O(14));
    mux_15: mux_vhd_x port map (S, D1(15), D0(15), O(15));
end default;

// VHDL entity mux4_vhd_x16, as the project stores it:
library IEEE;
use IEEE.std_logic_1164.all;

entity mux4_vhd_x16 is
    Port (
        S:  in  STD_LOGIC_VECTOR (1 downto 0);
        D3: in  STD_LOGIC_VECTOR (15 downto 0);
        D2: in  STD_LOGIC_VECTOR (15 downto 0);
        D1: in  STD_LOGIC_VECTOR (15 downto 0);
        D0: in  STD_LOGIC_VECTOR (15 downto 0);
        O:  out STD_LOGIC_VECTOR (15 downto 0)
    );
end mux4_vhd_x16;

architecture default of mux4_vhd_x16 is
    component mux_hdl_x16 is
        Port (
            S:  in  STD_LOGIC;
            D1: in  STD_LOGIC_VECTOR (15 downto 0);
            D0: in  STD_LOGIC_VECTOR (15 downto 0);
            O:  out STD_LOGIC_VECTOR (15 downto 0)
        );
    end component;

    signal H: STD_LOGIC_VECTOR (15 downto 0);
    signal L: STD_LOGIC_VECTOR (15 downto 0);

begin
    mux_h : mux_hdl_x16 port map (S(0), D3, D2, H);
    mux_l : mux_hdl_x16 port map (S(0), D1, D0, L);
    last  : mux_hdl_x16 port map (S(1), H, L, O);
end default;

// VHDL entity mux8_vhd_x16, as the project stores it:
library IEEE;
use IEEE.std_logic_1164.all;

entity mux8_vhd_x16 is
    Port (
        S   : in    STD_LOGIC_VECTOR (2 downto 0);
        D7  : in    STD_LOGIC_VECTOR (15 downto 0);
        D6  : in    STD_LOGIC_VECTOR (15 downto 0);
        D5  : in    STD_LOGIC_VECTOR (15 downto 0);
        D4  : in    STD_LOGIC_VECTOR (15 downto 0);
        D3  : in    STD_LOGIC_VECTOR (15 downto 0);
        D2  : in    STD_LOGIC_VECTOR (15 downto 0);
        D1  : in    STD_LOGIC_VECTOR (15 downto 0);
        D0  : in    STD_LOGIC_VECTOR (15 downto 0);
        O   : out   STD_LOGIC_VECTOR (15 downto 0)
    );
end mux8_vhd_x16;

architecture default of mux8_vhd_x16 is
    component mux_hdl_x16 is
        Port (
            S:  in  STD_LOGIC;
            D1: in  STD_LOGIC_VECTOR (15 downto 0);
            D0: in  STD_LOGIC_VECTOR (15 downto 0);
            O:  out STD_LOGIC_VECTOR (15 downto 0)
        );
    end component;
    component mux4_vhd_x16 is
        Port (
            S:  in  STD_LOGIC_VECTOR (1 downto 0);
            D3: in  STD_LOGIC_VECTOR (15 downto 0);
            D2: in  STD_LOGIC_VECTOR (15 downto 0);
            D1: in  STD_LOGIC_VECTOR (15 downto 0);
            D0: in  STD_LOGIC_VECTOR (15 downto 0);
            O:  out STD_LOGIC_VECTOR (15 downto 0)
        );
    end component;

    signal H: STD_LOGIC_VECTOR (15 downto 0);
    signal L: STD_LOGIC_VECTOR (15 downto 0);

begin
    get_high : mux4_vhd_x16 port map (S(1 downto 0), D7, D6, D5, D4, H);
    get_low  : mux4_vhd_x16 port map (S(1 downto 0), D3, D2, D1, D0, L);
    last     : mux_hdl_x16 port map (S(2), H, L, O);
end default;

// VHDL entity dmux_hdl_x16, as the project stores it:
library IEEE;
use IEEE.std_logic_1164.all;

entity dmux_hdl_x16 is
    Port (
        S:  in  STD_LOGIC;
        D1: in  STD_LOGIC_VECTOR (15 downto 0);
        D0: in  STD_LOGIC_VECTOR (15 downto 0);
        O:  out STD_LOGIC_VECTOR (15 downto 0)
    );
end dmux_hdl_x16;

architecture default of dmux_hdl_x16 is
    component dmux_vhd_x is
        Port (
            S   : in    STD_LOGIC;
            D1  : in    STD_LOGIC;
            D0  : in    STD_LOGIC;
            O   : out   STD_LOGIC
        );
    end component;

begin
    dmux_0: dmux_vhd_x port map (S, D1(0), D0(0), O(0));
    dmux_1: dmux_vhd_x port map (S, D1(1), D0(1), O(1));
    dmux_2: dmux_vhd_x port map (S, D1(2), D0(2), O(2));
    dmux_3: dmux_vhd_x port map (S, D1(3), D0(3), O(3));
    dmux_4: dmux_vhd_x port map (S, D1(4), D0(4), O(4));
    dmux_5: dmux_vhd_x port map (S, D1(5), D0(5), O(5));
    dmux_6: dmux_vhd_x port map (S, D1(6), D0(6), O(6));
    dmux_7: dmux_vhd_x port map (S, D1(7), D0(7), O(7));
    dmux_8: dmux_vhd_x port map (S, D1(8), D0(8), O(8));
    dmux_9: dmux_vhd_x port map (S, D1(9), D0(9), O(9));
    dmux_10: dmux_vhd_x port map (S, D1(10), D0(10), O(10));
    dmux_11: dmux_vhd_x port map (S, D1(11), D0(11), O(11));
    dmux_12: dmux_vhd_x port map (S, D1(12), D0(12), O(12));
    dmux_13: dmux_vhd_x port map (S, D1(13), D0(13), O(13));
    dmux_14: dmux_vhd_x port map (S, D1(14), D0(14), O(14));
    dmux_15: dmux_vhd_x port map (S, D1(15), D0(15), O(15));
end default;

// VHDL entity dmux_vhd_x16, as the project stores it:
library IEEE;
use IEEE.std_logic_1164.all;

entity dmux_vhd_x16 is
    Port (
        S:  in   STD_LOGIC;
        D:  in   STD_LOGIC_VECTOR (15 downto 0);
        O1: out  STD_LOGIC_VECTOR (15 downto 0);
        O0: out  STD_LOGIC_VECTOR (15 downto 0)
    );
end dmux_vhd_x16;

architecture default of dmux_vhd_x16 is
    component dmux_vhd_x is
        Port (
            S:  in   STD_LOGIC;
            D:  in   STD_LOGIC;
            O1: out  STD_LOGIC;
            O0: out  STD_LOGIC
        );
    end component;

begin
    dmux_0: dmux_vhd_x port map (S, D(0), O1(0), O0(0));
    dmux_1: dmux_vhd_x port map (S, D(1), O1(1), O0(1));
    dmux_2: dmux_vhd_x port map (S, D(2), O1(2), O0(2));
    dmux_3: dmux_vhd_x port map (S, D(3), O1(3), O0(3));
    dmux_4: dmux_vhd_x port map (S, D(4), O1(4), O0(4));
    dmux_5: dmux_vhd_x port map (S, D(5), O1(5), O0(5));
    dmux_6: dmux_vhd_x port map (S, D(6), O1(6), O0(6));
    dmux_7: dmux_vhd_x port map (S, D(7), O1(7), O0(7));
    dmux_8: dmux_vhd_x port map (S, D(8), O1(8), O0(8));
    dmux_9: dmux_vhd_x port map (S, D(9), O1(9), O0(9));
    dmux_10: dmux_vhd_x port map (S, D(10), O1(10), O0(10));
    dmux_11: dmux_vhd_x port map (S, D(11), O1(11), O0(11));
    dmux_12: dmux_vhd_x port map (S, D(12), O1(12), O0(12));
    dmux_13: dmux_vhd_x port map (S, D(13), O1(13), O0(13));
    dmux_14: dmux_vhd_x port map (S, D(14), O1(14), O0(14));
    dmux_15: dmux_vhd_x port map (S, D(15), O1(15), O0(15));
end default;

// VHDL entity dmux4_vhd_x16, as the project stores it:
library IEEE;
use IEEE.std_logic_1164.all;

entity dmux4_vhd_x16 is
    Port (
        S:  in   STD_LOGIC_VECTOR (1 downto 0);
        D:  in   STD_LOGIC_VECTOR (15 downto 0);
        O3: out  STD_LOGIC_VECTOR (15 downto 0);
        O2: out  STD_LOGIC_VECTOR (15 downto 0);
        O1: out  STD_LOGIC_VECTOR (15 downto 0);
        O0: out  STD_LOGIC_VECTOR (15 downto 0)
    );
end dmux4_vhd_x16;

architecture default of dmux4_vhd_x16 is
    component dmux_vhd_x16 is
        Port (
            S:  in   STD_LOGIC;
            D:  in   STD_LOGIC_VECTOR (15 downto 0);
            O1: out  STD_LOGIC_VECTOR (15 downto 0);
            O0: out  STD_LOGIC_VECTOR (15 downto 0)
        );
    end component;

    signal H: STD_LOGIC_VECTOR (15 downto 0);
    signal L: STD_LOGIC_VECTOR (15 downto 0);

begin
    locate      : dmux_vhd_x16 port map (S(1), D, H, L);
    output_high : dmux_vhd_x16 port map (S(0), H, O3, O2);
    output_low  : dmux_vhd_x16 port map (S(0), L, O1, O0);
end default;

// VHDL entity dmux8_vhd_x16, as the project stores it:
library IEEE;
use IEEE.std_logic_1164.all;

entity dmux8_vhd_x16 is
    Port (
        S:  in   STD_LOGIC_VECTOR (2 downto 0);
        D:  in   STD_LOGIC_VECTOR (15 downto 0);
        O7: out  STD_LOGIC_VECTOR (15 downto 0);
        O6: out  STD_LOGIC_VECTOR (15 downto 0);
        O5: out  STD_LOGIC_VECTOR (15 downto 0);
        O4: out  STD_LOGIC_VECTOR (15 downto 0);
        O3: out  STD_LOGIC_VECTOR (15 downto 0);
        O2: out  STD_LOGIC_VECTOR (15 downto 0);
        O1: out  STD_LOGIC_VECTOR (15 downto 0);
        O0: out  STD_LOGIC_VECTOR (15 downto 0)
    );
end dmux8_vhd_x16;

architecture default of dmux8_vhd_x16 is
    component dmux_vhd_x16 is
        Port (
            S:  in   STD_LOGIC;
            D:  in   STD_LOGIC_VECTOR (15 downto 0);
            O1: out  STD_LOGIC_VECTOR (15 downto 0);
            O0: out  STD_LOGIC_VECTOR (15 downto 0)
        );
    end component;
    component dmux4_vhd_x16 is
        Port (
            S:  in   STD_LOGIC_VECTOR (1 downto 0);
            D:  in   STD_LOGIC_VECTOR (15 downto 0);
            O3: out  STD_LOGIC_VECTOR (15 downto 0);
            O2: out  STD_LOGIC_VECTOR (15 downto 0);
            O1: out  STD_LOGIC_VECTOR (15 downto 0);
            O0: out  STD_LOGIC_VECTOR (15 downto 0)
        );
    end component;

    signal H: STD_LOGIC_VECTOR (15 downto 0);
    signal L: STD_LOGIC_VECTOR (15 downto 0);

begin
    locate      : dmux_vhd_x16 port map (S(2), D, H, L);
    output_high : dmux4_vhd_x16 port map (S(1 downto 0), H, O7, O6, O5, O4);
    output_low  : dmux4_vhd_x16 port map (S(1 downto 0), L, O3, O2, O1, O0);
end default;
