// Logisim project mem.circ as structural Verilog
module sr_latch (
  input  S,
  input  R,
  output out_3
);

  wire nand_1_out;

  nand nand_1 (nand_1_out, S, out_3);
  nand nand_2 (out_3, nand_1_out, R);
endmodule

module d_latch (
  input  st,
  input  d,
  output out_3
);

  wire and_x_1_out_3, and_x_2_out_3, not_x_1_out_2, not_x_2_out_2, not_x_3_out_2;

  and_x and_x_1 (.in_1(st), .in_2(not_x_1_out_2), .out_3(and_x_1_out_3));
  not_x not_x_1 (.in_1(d), .out_2(not_x_1_out_2));
  and_x and_x_2 (.in_1(st), .in_2(d), .out_3(and_x_2_out_3));
  not_x not_x_2 (.in_1(and_x_1_out_3), .out_2(not_x_2_out_2));
  not_x not_x_3 (.in_1(and_x_2_out_3), .out_2(not_x_3_out_2));
  sr_latch sr_latch_1 (.S(not_x_2_out_2), .R(not_x_3_out_2), .out_3(out_3));
endmodule

module dff (
  input  d,
  input  in_2,
  output out_3
);

  wire and_x_1_out_3, d_ff_1_q, not_x_1_out_2;

  and_x and_x_1 (.in_1(in_2), .in_2(in_2), .out_3(and_x_1_out_3));
  not_x not_x_1 (.in_1(in_2), .out_2(not_x_1_out_2));
  D_Flip_Flop d_ff_1 (.D(d), .clk(and_x_1_out_3), .Q(d_ff_1_q));  // open: Qn, preset, reset
  D_Flip_Flop d_ff_2 (.D(d_ff_1_q), .clk(not_x_1_out_2), .Q(out_3));  // open: Qn, preset, reset

  // Notes on the sheet:
  //   clk
  //   st
endmodule

module reg_x16 (
  input  in_1,
  input  load,
  input  [15:0] data,
  output [15:0] out_4
);

  wire [15:0] mux_x16_1_out_4;

  mux_x16 mux_x16_1 (.in_1(load), .in_2(data), .in_3(out_4), .out_4(mux_x16_1_out_4));
  dff dff_1 (.d(mux_x16_1_out_4[0]), .in_2(in_1), .out_3(out_4[0]));
  dff dff_2 (.d(mux_x16_1_out_4[1]), .in_2(in_1), .out_3(out_4[1]));
  dff dff_3 (.d(mux_x16_1_out_4[2]), .in_2(in_1), .out_3(out_4[2]));
  dff dff_4 (.d(mux_x16_1_out_4[3]), .in_2(in_1), .out_3(out_4[3]));
  dff dff_5 (.d(mux_x16_1_out_4[4]), .in_2(in_1), .out_3(out_4[4]));
  dff dff_6 (.d(mux_x16_1_out_4[5]), .in_2(in_1), .out_3(out_4[5]));
  dff dff_7 (.d(mux_x16_1_out_4[6]), .in_2(in_1), .out_3(out_4[6]));
  dff dff_8 (.d(mux_x16_1_out_4[7]), .in_2(in_1), .out_3(out_4[7]));
  dff dff_9 (.d(mux_x16_1_out_4[8]), .in_2(in_1), .out_3(out_4[8]));
  dff dff_10 (.d(mux_x16_1_out_4[9]), .in_2(in_1), .out_3(out_4[9]));
  dff dff_11 (.d(mux_x16_1_out_4[10]), .in_2(in_1), .out_3(out_4[10]));
  dff dff_12 (.d(mux_x16_1_out_4[11]), .in_2(in_1), .out_3(out_4[11]));
  dff dff_13 (.d(mux_x16_1_out_4[12]), .in_2(in_1), .out_3(out_4[12]));
  dff dff_14 (.d(mux_x16_1_out_4[13]), .in_2(in_1), .out_3(out_4[13]));
  dff dff_15 (.d(mux_x16_1_out_4[14]), .in_2(in_1), .out_3(out_4[14]));
  dff dff_16 (.d(mux_x16_1_out_4[15]), .in_2(in_1), .out_3(out_4[15]));

  // Other names for the same wires on the sheet: CLK = in_1
endmodule

module pc_x16 (
  input  in_1,
  input  load,
  input  [15:0] in_3,
  output [15:0] out_4
);

  wire not_x_1_out_2;
  wire [15:0] inc_x16_1_out_2, mux_x16_1_out_4;

  not_x not_x_1 (.in_1(in_1), .out_2(not_x_1_out_2));
  reg_x16 reg_x16_1 (.in_1(in_1), .load(not_x_1_out_2), .data(mux_x16_1_out_4), .out_4(out_4));
  mux_x16 mux_x16_1 (.in_1(load), .in_2(in_3), .in_3(inc_x16_1_out_2), .out_4(mux_x16_1_out_4));
  inc_x16 inc_x16_1 (.in_1(out_4), .out_2(inc_x16_1_out_2));

  // Notes on the sheet:
  //   data
  //   clk
endmodule

module ram8_x16 (
  input  [2:0] in_1,
  input  load,
  input  [15:0] in_3,
  input  clk,
  output [15:0] out
);

  wire dmux8_1_out_3, dmux8_1_out_4, dmux8_1_out_5, dmux8_1_out_6, dmux8_1_out_7, dmux8_1_out_8,
       dmux8_1_out_9, dmux8_1_out_10;
  wire [15:0] reg_x16_1_out_4, reg_x16_2_out_4, reg_x16_3_out_4, reg_x16_4_out_4, reg_x16_5_out_4,
       reg_x16_6_out_4, reg_x16_7_out_4, reg_x16_8_out_4;

  dmux8 dmux8_1 (
    .in_2(load), .in_1(in_1), .out_4(dmux8_1_out_4), .out_5(dmux8_1_out_5), .out_6(dmux8_1_out_6),
    .out_7(dmux8_1_out_7), .out_8(dmux8_1_out_8), .out_9(dmux8_1_out_9), .out_10(dmux8_1_out_10),
    .out_3(dmux8_1_out_3));
  reg_x16 reg_x16_1 (.load(dmux8_1_out_3), .data(in_3), .out_4(reg_x16_1_out_4));  // open: in_1
  reg_x16 reg_x16_2 (.in_1(clk), .load(dmux8_1_out_4), .data(in_3), .out_4(reg_x16_2_out_4));
  reg_x16 reg_x16_3 (.in_1(clk), .load(dmux8_1_out_5), .data(in_3), .out_4(reg_x16_3_out_4));
  reg_x16 reg_x16_4 (.in_1(clk), .load(dmux8_1_out_6), .data(in_3), .out_4(reg_x16_4_out_4));
  reg_x16 reg_x16_5 (.in_1(clk), .load(dmux8_1_out_7), .data(in_3), .out_4(reg_x16_5_out_4));
  reg_x16 reg_x16_6 (.in_1(clk), .load(dmux8_1_out_8), .data(in_3), .out_4(reg_x16_6_out_4));
  reg_x16 reg_x16_7 (.in_1(clk), .load(dmux8_1_out_9), .data(in_3), .out_4(reg_x16_7_out_4));
  reg_x16 reg_x16_8 (.in_1(clk), .load(dmux8_1_out_10), .data(in_3), .out_4(reg_x16_8_out_4));
  mux8_x16 ReadControl (
    .in_9(in_1), .in_1(reg_x16_1_out_4), .in_2(reg_x16_2_out_4), .in_3(reg_x16_3_out_4),
    .in_4(reg_x16_4_out_4), .in_5(reg_x16_5_out_4), .in_6(reg_x16_6_out_4), .in_7(reg_x16_7_out_4),
    .in_8(reg_x16_8_out_4), .out_10(out));

  // Other names for the same wires on the sheet: data[15:0] = in_3

  // Notes on the sheet:
  //   address
  //   data
  //   0x0007
  //   0x0006
  //   0x0005
  //   0x0004
  //   0x0003
  //   0x0002
  //   0x0001
  //   0x0000
endmodule

module ram64_x16 (
  input  [5:0] in_1,
  input  load,
  input  [15:0] in_3,
  input  clk,
  output [15:0] out
);

  wire dmux8_1_out_3, dmux8_1_out_4, dmux8_1_out_5, dmux8_1_out_6, dmux8_1_out_7, dmux8_1_out_8,
       dmux8_1_out_9, dmux8_1_out_10;
  wire [15:0] ram8_x16_1_out, ram8_x16_2_out, ram8_x16_3_out, ram8_x16_4_out, ram8_x16_5_out, ram8_x16_6_out,
       ram8_x16_7_out, ram8_x16_8_out;

  dmux8 dmux8_1 (
    .in_2(load), .in_1(in_1[5:3]), .out_4(dmux8_1_out_4), .out_5(dmux8_1_out_5), .out_6(dmux8_1_out_6),
    .out_7(dmux8_1_out_7), .out_8(dmux8_1_out_8), .out_9(dmux8_1_out_9), .out_10(dmux8_1_out_10),
    .out_3(dmux8_1_out_3));
  ram8_x16 ram8_x16_1 (.load(dmux8_1_out_3), .clk(clk), .in_1(in_1[2:0]), .in_3(in_3), .out(ram8_x16_1_out));
  ram8_x16 ram8_x16_2 (.load(dmux8_1_out_4), .clk(clk), .in_1(in_1[2:0]), .in_3(in_3), .out(ram8_x16_2_out));
  ram8_x16 ram8_x16_3 (.load(dmux8_1_out_5), .clk(clk), .in_1(in_1[2:0]), .in_3(in_3), .out(ram8_x16_3_out));
  ram8_x16 ram8_x16_4 (.load(dmux8_1_out_6), .clk(clk), .in_1(in_1[2:0]), .in_3(in_3), .out(ram8_x16_4_out));
  ram8_x16 ram8_x16_5 (.load(dmux8_1_out_7), .clk(clk), .in_1(in_1[2:0]), .in_3(in_3), .out(ram8_x16_5_out));
  ram8_x16 ram8_x16_6 (.load(dmux8_1_out_8), .clk(clk), .in_1(in_1[2:0]), .in_3(in_3), .out(ram8_x16_6_out));
  ram8_x16 ram8_x16_7 (.load(dmux8_1_out_9), .clk(clk), .in_1(in_1[2:0]), .in_3(in_3), .out(ram8_x16_7_out));
  ram8_x16 ram8_x16_8 (.load(dmux8_1_out_10), .clk(clk), .in_1(in_1[2:0]), .in_3(in_3), .out(ram8_x16_8_out));
  mux8_x16 ReadControl (
    .in_9(in_1[5:3]), .in_1(ram8_x16_1_out), .in_2(ram8_x16_2_out), .in_3(ram8_x16_3_out),
    .in_4(ram8_x16_4_out), .in_5(ram8_x16_5_out), .in_6(ram8_x16_6_out), .in_7(ram8_x16_7_out),
    .in_8(ram8_x16_8_out), .out_10(out));

  // Other names for the same wires on the sheet: data[15:0] = in_3; addr_L3[2:0] = in_1[2:0]

  // Notes on the sheet:
  //   address
  //   data
endmodule
